# Fritzing sketch alarm clock project (saved by Fritzing 1.0.5)
breadboards: 1
stripboards: 2

parts:
  pi = Raspberry Pi Pico W
  SP2 = SPEAKER [package=pcb_mount_speaker]
  L9110h1 = DIP - 8 pins [part_number=L9110H chip_label=L9110h package="DIP (Dual Inline) [THT]"]
  Q1 = NPN-Transistor [package="TO92 [THT]"]
  DFPlayer_Mini1 = DFPlayer MINI [package="DIP (Dual Inline) [THT]"]
  M2 = OLED Mono 2.42 inch green
  M3 = DC Motor [voltage_(max)=6V voltage_(min)=3V]
  U1 = LIPO-110mAh [package=lipo-110]  # not connected
  Part2 = Adafruit TMP117
  R6 = Resistor [tolerance=±5% power=0.25W resistance=1000 package=THT]
  D3 = Rectifier Diode [part_number=1N4001 package="300 mil [THT]"]
  Part3 = PowerBoost 500 Charger
  R8 = Resistor [tolerance=±5% power=0.25W resistance=10000 package=THT]
  R9 = Resistor [tolerance=±5% power=0.25W resistance=10000 package=THT]
  A1 = mini boost module
  S1 = Pushbutton [package="[THT]"]
  LED1 = LED - 5mm [color="White (4500K)" current=0.030A package="5 mm [THT]"]
  LED2 = LED - 5mm [color="White (4500K)" current=0.030A package="5 mm [THT]"]
  LED3 = LED - 5mm [color="White (4500K)" current=0.030A package="5 mm [THT]"]
  LED4 = LED - 5mm [color="White (4500K)" current=0.030A package="5 mm [THT]"]
  R10 = Resistor [tolerance=±5% power=0.25W resistance=100 package=THT]
  R11 = Resistor [tolerance=±5% power=0.25W resistance=100 package=THT]
  R12 = Resistor [tolerance=±5% power=0.25W resistance=10k package=THT]
  R13 = Resistor [tolerance=±5% power=0.25W resistance=10k package=THT]
  Q4 = NPN-Transistor [package="TO92 [THT]"]
  Q5 = NPN-Transistor [package="TO92 [THT]"]

nets:
  GND: pi.pin_3, pi.pin_8, pi.pin_13, pi.pin_18, pi.pin_23, pi.pin_28, pi.pin_33, pi.pin_38, pi.pin_42, L9110h1.GND, DFPlayer_Mini1.GND#9, M2.GND, Part2.GND, Part3.GND, R8.Pin_1, A1.Pin_1, S1.Pin_1, S1.Pin_2
  N1: pi.pin_15, M2.CS
  N2: pi.pin_16, M2.DC
  N3: pi.pin_17, M2.RES
  N4: pi.pin_19, M2.SCK
  N5: pi.pin_20, M2.SDA
  N6: pi.pin_21, DFPlayer_Mini1.RX
  N7: pi.pin_22, DFPlayer_Mini1.TX
  N8: pi.pin_24, L9110h1.IB
  N9: pi.pin_25, L9110h1.IA
  N10: pi.pin_26, DFPlayer_Mini1.BUSY
  N11: pi.pin_27, Q1.B
  N12: pi.pin_30, S1.Pin_3, S1.Pin_4
  N13: pi.pin_31, Part2.SDA
  N14: pi.pin_32, Part2.SCL
  N15: pi.pin_34, R6.Pin_1
  N16: pi.pin_36, Part2.VCC
  N17: pi.pin_39, D3.cathode
  N18: SP2.+, Q1.C
  N19: SP2.-, DFPlayer_Mini1.SPK1
  N20: L9110h1.OA, M3.pin_1
  N21: L9110h1.OB, M3.pin_2
  N22: Q1.E, DFPlayer_Mini1.SPK2
  VCC: DFPlayer_Mini1.VCC, M2.VCC
  N23: R6.Pin_0, R8.Pin_0, R9.Pin_1
  N24: D3.anode, Part3.5.0V, A1.Pin_2
  N25: Part3.VBAT, R9.Pin_0
  N26: A1.Pin_3, Q4.E, Q5.E
  N27: A1.Pin_4, R10.Pin_0, R11.Pin_0
  N28: LED1.cathode, R11.Pin_1
  N29: LED2.anode, Q4.C
  N30: LED3.anode, Q5.C
  N31: LED4.cathode, R10.Pin_1
  N32: R12.Pin_1, Q5.B
  N33: R13.Pin_1, Q4.B

notes:
  it's actually 1200mah LiPoly
  buttons
  motor was removed
  boost to 9v

custom parts:
  Raspberry Pi Pico W: Raspberry Pi Pico W. Based around the RP2040 microcontroller the Pico W is a low cost microcontroller device bringing Raspberry Pi quality, cost, and easy of use to the microcontroller space. The areas marked KEEPOUT in pcb silkscreen should not have traces running through them to avoid shorts on a soldered in module!
  DIP - 8 pins: A DIP stand-in part for whatever IC you want. With 8 pins on a 300mil dual inline package (DIP) footprint.
  DFPlayer MINI: MP3 module by DFRobot.com for playing Music from an SD-Card. Supports WAV and MP3 files.
  OLED Mono 2.42 inch green: This is a 2.42 inch OLED display module of 128x64 resolution.
  Adafruit TMP117: The TMP117 Precision Temperature Sensor is an I2C temperature sensor that will help you easily add temperature measurement and adjustment to your project. In addition to the obvious support for reading the temperature, the TMP117 can also monitor the temperature and alert you when corrective action needs to be taken. With 16-bit measurement resolution and ±0.1°C accuracy, as well as high and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
  PowerBoost 500 Charger: The PowerBoost 500C is a little DC/DC boost converter module that can be powered by any 3.7V LiIon/LiPoly battery, and convert the battery output to 5.2V DC for running your 5V projects. At its heart is a TPS61090 boost converter from TI. This boost converter chip has some really nice extras such as low battery detection, 2A internal switch, synchronous conversion, excellent efficiency, and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
  mini boost module: mini boost module.
